# Fritzing sketch ExternalLight_SchematicFull (saved by Fritzing 0.9.4)
breadboards: 1

parts:
  Part1 = Arduino Nano (Rev3.0)
  Part2 = Bluetooth HC-05 Macho
  R1 = Resistor [tolerance=±5% resistance=2k package=THT]
  R2 = Resistor [tolerance=±5% resistance=1k package=THT]
  R3 = Resistor [tolerance=±5% resistance=560 package=THT]
  LED1 = LED - 3mm [color="Red (633nm)" package="3 mm [THT]"]
  VCC1 = Battery block 9V
  M1 = RioRand LM2596
  Q1 = NPN-Transistor [package="SOT-23 [SMD]"]
  Q2 = NPN-Transistor [package="SOT-23 [SMD]"]
  Q3 = NPN-Transistor [package="SOT-23 [SMD]"]
  LED2 = smd LED [color="Red (633nm)" package="0603 [SMD]"]
  LED3 = smd LED [color="Red (633nm)" package="0603 [SMD]"]
  LED4 = smd LED [color="Red (633nm)" package="0603 [SMD]"]
  Q4 = Basic FET N-Channel [package="TO220 [THT]"]
  R4 = Resistor [tolerance=±5% resistance=50 package=THT]
  R5 = Resistor [tolerance=±5% resistance=10k package=THT]

nets:
  N1: Part1.D2, Part2.TXD
  N2: Part1.D3, R1.Pin_1, R2.Pin_0
  N3: Part1.D4, LED1.cathode
  N4: Part1.D6, Q4.gate, R5.Pin_0
  VIN: Part1.VIN, Part2.VCC, M1.Pin_3
  GND: Part1.GND, Part2.GND, R1.Pin_0, R3.Pin_1, M1.Pin_4, Q4.source, R5.Pin_1
  N5: Part2.RXD, R2.Pin_1
  N6: R3.Pin_0, LED1.anode
  N7: VCC1.+, LED2.cathode, LED3.cathode, LED4.cathode
  N8: Q1.2, Q2.2, Q3.2, R4.Pin_0
  N9: Q1.0, Q2.0, Q3.0, Q3.1, LED2.anode
  N10: Q1.1, LED4.anode
  N11: Q2.1, LED3.anode
  N12: Q4.drain, R4.Pin_1

notes:
  Represents 12V/2A power supply
  12V, 10W Power LEDs
