# Fritzing sketch MainAlarm_SchematicFull (saved by Fritzing 0.9.4)
breadboards: 1

parts:
  Arduino = Arduino Mega ADK (Rev3)
  R1 = Resistor [tolerance=±5% resistance=4.7 package=THT]
  Q1 = NPN-Transistor [package="TO92 [THT]"]
  J1 = Active buzzer
  J2 = Active buzzer
  J3 = Active buzzer
  Part1 = Bluetooth HC-05 Macho
  R2 = Resistor [tolerance=±5% resistance=2k package="2010 [SMD]"]
  R3 = Resistor [tolerance=±5% resistance=1k package="2010 [SMD]"]
  S1 = Round Pushbutton
  R4 = Resistor [tolerance=±5% resistance=10k package=THT]
  Matrix_keypad1 = KEYPAD 4x4
  LCM1602_IIC1 = LCM1602 IIC [part_number="LCM1602 IIC" chip_label="LCM1602 IIC" package="DIP (Dual Inline) [THT]"]
  LCD1 = LCD screen

nets:
  N1: Arduino.D21/SCL, LCM1602_IIC1.SCL
  N2: Arduino.D20/SDA, LCM1602_IIC1.SDA
  VCC: Arduino.5V, J1.pin2, J3.pin2, Part1.VCC, S1.leg1, LCM1602_IIC1.VCC
  GND: Arduino.GND, Q1.E, Part1.GND, R2.Pin_0, R4.Pin_1, LCM1602_IIC1.GND
  N3: Arduino.D2_PWM, R1.Pin_0
  N4: Arduino.D3_PWM, S1.leg0, R4.Pin_0
  N5: Arduino.D42, Part1.TXD
  N6: Arduino.D43, R3.Pin_1
  N7: Arduino.D46, Matrix_keypad1.row4
  N8: Arduino.D47, Matrix_keypad1.row3
  N9: Arduino.D48, Matrix_keypad1.row2
  N10: Arduino.D49, Matrix_keypad1.row1
  N11: Arduino.D50/MISO, Matrix_keypad1.col4
  N12: Arduino.D51/MOSI, Matrix_keypad1.col3
  N13: Arduino.D52/SCK, Matrix_keypad1.col2
  N14: Arduino.D53/SS, Matrix_keypad1.col1
  N15: R1.Pin_1, Q1.B
  N16: Q1.C, J1.pin1, J2.pin2, J3.pin1
  N17: Part1.RXD, R2.Pin_1, R3.Pin_0
  VSS: LCM1602_IIC1.VSS, LCD1.VSS
  VDD: LCM1602_IIC1.VDD, LCD1.VDD
  N18: LCM1602_IIC1.V0, LCD1.V0
  N19: LCM1602_IIC1.RS, LCD1.RS
  N20: LCM1602_IIC1.RW, LCD1.R/W
  N21: LCM1602_IIC1.E, LCD1.E
  N22: LCM1602_IIC1.D0, LCD1.DB0
  N23: LCM1602_IIC1.D1, LCD1.DB1
  N24: LCM1602_IIC1.D2, LCD1.DB2
  N25: LCM1602_IIC1.D3, LCD1.DB3
  N26: LCM1602_IIC1.D4, LCD1.DB4
  N27: LCM1602_IIC1.D5, LCD1.DB5
  N28: LCM1602_IIC1.D6, LCD1.DB6
  N29: LCM1602_IIC1.D7, LCD1.DB7
  N30: LCM1602_IIC1.A, LCD1.LED+
  N31: LCM1602_IIC1.K, LCD1.LED-

notes:
  Represents 16x4 LCD

custom parts:
  KEYPAD 4x4: Matrix keypad 16 buttons, 4 rows x 4 columns
  LCM1602 IIC: I2C-Module to use a 1602 or 2004 LCD on with the wire.h libory Serial LCD Modul
