# Fritzing sketch active_buzzer_schematic (saved by Fritzing 0.9.4)
breadboards: 1

parts:
  Part1 = Arduino Mega ADK (Rev3)
  Q1 = TRANSISTOR_NPN [package=to-92-ammo]
  J1 = Piezo Speaker
  J2 = Piezo Speaker
  J3 = Piezo Speaker
  R1 = Resistor [tolerance=±5% resistance=70 package="0402 [SMD]"]

nets:
  N1: Part1.GND, R1.Pin_0
  N2: Part1.IOREF, Part1.5V, J1.pin2, J2.pin2, J3.pin2
  N3: Part1.D2_PWM, Q1.B
  N4: Q1.E, R1.Pin_1
  N5: Q1.C, J1.pin1, J2.pin1, J3.pin1
