# Fritzing sketch LCD display schematic (saved by Fritzing 0.9.4)
breadboards: 1

parts:
  LCD1 = LCD screen
  Arduino = Arduino Uno (Rev3) - ICSP
  R1 = Resistor [tolerance=±5% resistance=220 package=THT]

nets:
  VSS: LCD1.VSS, LCD1.V0, LCD1.R/W, LCD1.LED-, Arduino.GND
  VDD: LCD1.VDD, Arduino.5V
  N1: LCD1.RS, Arduino.D12/MISO
  N2: LCD1.E, Arduino.ICSP_MOSI, Arduino.D11_PWM/MOSI
  N3: LCD1.DB4, Arduino.D1/TX
  N4: LCD1.DB5, Arduino.D2
  N5: LCD1.DB6, Arduino.D3_PWM
  N6: LCD1.DB7, Arduino.D4
  N7: LCD1.LED+, R1.Pin_1
  N8: Arduino.D9_PWM, R1.Pin_0
